# Fritzing sketch CircuitDesign01 (saved by Fritzing 0.9.4)

parts:
  Part1 = Arduino Leonardo (Rev3b)
  LED1 = smd LED [color="Red (633nm)" package="0805 [SMD]"]
  S1 = Pushbutton [package="[THT]"]

nets:
  N1: Part1.3V3, S1.Pin_1, S1.Pin_2
  N2: Part1.GND, LED1.cathode
  N3: LED1.anode, S1.Pin_3
