# Fritzing sketch Untitled Sketch02 fx (saved by Fritzing 0.9.4)
breadboards: 1

parts:
  Part1 = Arduino Uno (Rev3)
  LED1 = LED - 3mm [color="Red (633nm)" package="3 mm [THT]"]
  R3 = Resistor [tolerance=±5% resistance=220 package=THT]
  R2 = Resistor [tolerance=±5% resistance=220 package=THT]
  R1 = Resistor [tolerance=±5% resistance=220 package=THT]

nets:
  N1: Part1.GND, LED1.cathode
  N2: Part1.3V3, R3.Pin_1, R2.Pin_1, R1.Pin_1
  N3: LED1.anode, R3.Pin_0, R2.Pin_0, R1.Pin_0
