# Fritzing sketch LEDWithButton (saved by Fritzing 0.9.3b)
breadboards: 2

parts:
  MCU = Arduino Uno (Rev3) - ICSP
  LED1 = LED - 5mm [color="Red (633nm)" package="5 mm [THT]"]
  R1 = Resistor [tolerance=±5% resistance=220 package=THT]
  R2 = Resistor [tolerance=±5% resistance=2.2k package=THT]
  R3 = Resistor [tolerance=±5% resistance=2.2k package=THT]
  R4 = Resistor [tolerance=±5% resistance=2.2k package=THT]
  R5 = Resistor [tolerance=±5% resistance=2.2k package=THT]
  R6 = Resistor [tolerance=±5% resistance=2.2k package=THT]
  S1 = Pushbutton [package="[THT]"]

nets:
  N1: MCU.D8, R1.Pin_1
  N2: MCU.D7, R6.Pin_1, S1.Pin_3, S1.Pin_4
  N3: MCU.5V, R2.Pin_0
  N4: MCU.GND, LED1.cathode, S1.Pin_1, S1.Pin_2
  N5: LED1.anode, R1.Pin_0
  N6: R2.Pin_1, R3.Pin_0
  N7: R3.Pin_1, R4.Pin_0
  N8: R4.Pin_1, R5.Pin_0
  N9: R5.Pin_1, R6.Pin_0
