# Fritzing sketch I2C (saved by Fritzing 0.9.3b)
breadboards: 1

parts:
  元件1 = Arduino Uno (Rev3)
  元件2 = Arduino Mega 2560 (Rev3)
  R1 = Resistor [tolerance=±5% resistance=2.2 package=THT]
  R2 = Resistor [tolerance=±5% resistance=2.2 package=THT]

nets:
  N1: 元件1.A4/SDA, 元件2.D20/SDA, 元件2.SDA, R1.Pin_1
  N2: 元件1.A5/SCL, 元件2.D21/SCL, 元件2.SCL, R2.Pin_1
  N3: 元件1.5V, R1.Pin_0, R2.Pin_0
  GND: 元件1.GND, 元件2.GND
